// Logisim project var1.circ as structural Verilog: 3 circuits, main circuit 1-1
module _1_1 (
  input  X0,
  input  X1,
  input  X2,
  input  X3,
  input  X4,
  output Y
);

  wire and_1_out, and_2_out, and_3_out, and_4_out, and_5_out, and_6_out, and_7_out, and_8_out, and_9_out,
       and_10_out, and_11_out, and_12_out, and_13_out, and_14_out, and_15_out, or_1_out, or_2_out, or_4_out;

  and and_1 (and_1_out, X1, X2);
  and and_2 (and_2_out, X3, X4);
  and and_3 (and_3_out, X0, X2);
  and and_4 (and_4_out, X3, X4);
  and and_5 (and_5_out, and_1_out, and_2_out);
  and and_6 (and_6_out, and_3_out, and_4_out);
  and and_7 (and_7_out, X0, X1);
  and and_8 (and_8_out, X3, X4);
  and and_9 (and_9_out, X0, X1);
  and and_10 (and_10_out, X2, X4);
  and and_11 (and_11_out, X0, X1);
  and and_12 (and_12_out, X2, X3);
  or or_1 (or_1_out, and_5_out, and_6_out);
  and and_13 (and_13_out, and_7_out, and_8_out);
  and and_14 (and_14_out, and_9_out, and_10_out);
  and and_15 (and_15_out, and_11_out, and_12_out);
  or or_2 (or_2_out, or_1_out, and_13_out);
  or or_3 (Y, or_2_out, or_4_out);
  or or_4 (or_4_out, and_14_out, and_15_out);
endmodule

module _1_2 (
  input  X1,
  input  X2,
  input  X3,
  output Y
);

  wire and_1_out, and_2_out, and_3_out, and_4_out, nand_1_out, nor_1_out, not_1_out, not_2_out;

  not not_1 (not_1_out, X2);
  not not_2 (not_2_out, X1);
  and and_1 (and_1_out, not_1_out, X1);
  and and_2 (and_2_out, X3, not_2_out);
  and and_3 (and_3_out, X3, X2);
  nor nor_1 (nor_1_out, and_1_out, and_2_out);
  nand nand_1 (nand_1_out, and_3_out, X1);
  and and_4 (and_4_out, X3, nor_1_out);
  nor nor_2 (Y, nand_1_out, and_4_out);
endmodule

module _1_3 (
  input  X3,
  input  X2,
  input  X1,
  input  X0,
  output Y
);

  wire and_1_out, and_2_out, and_3_out, and_4_out, and_5_out, and_6_out, and_7_out, and_8_out, and_9_out,
       and_10_out, not_1_out, not_2_out, not_3_out, not_4_out, not_5_out, not_6_out, not_7_out, not_8_out,
       not_9_out, not_10_out, or_1_out, or_2_out, or_3_out;

  not not_1 (not_1_out, X3);
  and and_1 (and_1_out, not_1_out, not_2_out);
  not not_2 (not_2_out, X1);
  not not_3 (not_3_out, X0);
  not not_4 (not_4_out, X3);
  and and_2 (and_2_out, not_4_out, not_5_out);
  not not_5 (not_5_out, X2);
  not not_6 (not_6_out, X2);
  not not_7 (not_7_out, X3);
  not not_8 (not_8_out, X1);
  and and_3 (and_3_out, and_1_out, not_3_out);
  and and_4 (and_4_out, and_2_out, X1);
  and and_5 (and_5_out, not_6_out, X1);
  not not_9 (not_9_out, X0);
  and and_6 (and_6_out, not_7_out, X2);
  not not_10 (not_10_out, X1);
  and and_7 (and_7_out, X3, not_8_out);
  or or_1 (or_1_out, and_3_out, and_4_out);
  and and_8 (and_8_out, and_5_out, not_9_out);
  and and_9 (and_9_out, and_6_out, not_10_out);
  and and_10 (and_10_out, and_7_out, X0);
  or or_2 (or_2_out, or_1_out, and_8_out);
  or or_3 (or_3_out, and_9_out, and_10_out);
  or or_4 (Y, or_2_out, or_3_out);
endmodule
