// Logisim project lab10.circ as structural Verilog: 1 circuit, main circuit 3
module _3 (
  input  in_1,
  input  in_2,
  input  in_3,
  input  in_4,
  input  C,
  input  C_2,
  input  C_3,
  input  Cy,
  input  C_4,
  input  Cy_2,
  input  C_5,
  input  C_6,
  input  Cy_3,
  input  C_7,
  input  C_8,
  input  C_9,
  input  C_10,
  output Q0,
  output Q1,
  output Q2,
  output Q3,
  output Q0_2,
  output Q1_2,
  output Q2_2,
  output Q3_2,
  output Q0_3,
  output Q1_3,
  output Q2_3,
  output Q0_4,
  output Q1_4,
  output Q2_4,
  output Q3_3,
  output Q0_5,
  output Q1_5,
  output Q2_5,
  output Q3_4,
  output Q0_6,
  output Q1_6,
  output Q2_6,
  output Q3_5,
  output Q0_7,
  output Q1_7,
  output Q2_7,
  output Q3_6,
  output Q4,
  output Q0_8,
  output Q1_8,
  output Q2_8,
  output Q3_7,
  output Q4_2,
  output Q0_9,
  output Q1_9,
  output Q2_9,
  output Q3_8,
  output Q4_3,
  output Q0_10,
  output Q1_10,
  output Q2_10,
  output Q3_9
);

  wire and_1_out, and_2_out, and_3_out, and_4_out, and_5_out, and_6_out, and_7_out, d_ff_1_qn, d_ff_2_qn,
       d_ff_3_qn, d_ff_4_qn, d_ff_5_qn, d_ff_6_qn, d_ff_7_qn, d_ff_8_qn, d_ff_9_qn, d_ff_10_qn, d_ff_11_qn,
       d_ff_12_qn, d_ff_13_qn, d_ff_14_qn, j_k_ff_1_qn, j_k_ff_2_qn, j_k_ff_3_qn, j_k_ff_4_qn, j_k_ff_5_qn,
       j_k_ff_6_qn, j_k_ff_7_qn, j_k_ff_8_qn, j_k_ff_9_qn, j_k_ff_10_q, j_k_ff_10_qn, j_k_ff_11_qn,
       j_k_ff_12_qn, j_k_ff_13_qn, s_r_ff_1_q, s_r_ff_1_qn, t_ff_1_qn, t_ff_4_qn, t_ff_5_qn, t_ff_10_qn,
       t_ff_11_qn, t_ff_14_qn;

  D_Flip_Flop d_ff_1 (.clk(in_1), .D(d_ff_1_qn), .Qn(d_ff_1_qn));  // open: Q, preset, en, reset
  D_Flip_Flop d_ff_2 (.clk(C_2), .D(d_ff_2_qn), .Q(Q0_2), .Qn(d_ff_2_qn), .reset(and_3_out));  // open: preset, en
  J_K_Flip_Flop j_k_ff_1 (
    .J(j_k_ff_1_qn), .clk(C_3), .K(Q0_3), .Q(Q0_3), .Qn(j_k_ff_1_qn), .preset(Cy));  // open: en, reset
  T_Flip_Flop t_ff_1 (.clk(C_4), .T(1'b1), .Q(Q0_4), .Qn(t_ff_1_qn), .preset(Cy_2));  // open: reset, en
  J_K_Flip_Flop j_k_ff_2 (
    .J(j_k_ff_2_qn), .clk(C_5), .K(Q0_5), .Q(Q0_5), .Qn(j_k_ff_2_qn), .reset(and_4_out));  // open: preset, en
  D_Flip_Flop d_ff_3 (.clk(C_6), .D(d_ff_3_qn), .Q(Q0_6), .Qn(d_ff_3_qn), .preset(Cy_3));  // open: en, reset
  T_Flip_Flop t_ff_2 (.clk(C_7), .T(1'b1), .Q(Q0_7), .preset(and_5_out));  // open: Qn, reset, en
  D_Flip_Flop d_ff_4 (.clk(C_8), .D(d_ff_4_qn), .Q(Q0_8), .Qn(d_ff_4_qn), .preset(and_6_out));  // open: en, reset
  J_K_Flip_Flop j_k_ff_3 (
    .J(j_k_ff_3_qn), .clk(C_9), .K(Q0_9), .Q(Q0_9), .Qn(j_k_ff_3_qn), .preset(and_7_out));  // open: en, reset
  T_Flip_Flop t_ff_3 (.clk(C_10), .T(1'b1), .Q(Q0_10), .preset(and_1_out));  // open: Qn, reset, en
  S_R_Flip_Flop s_r_ff_1 (
    .S(s_r_ff_1_qn), .clk(in_3), .R(s_r_ff_1_q), .Q(s_r_ff_1_q), .Qn(s_r_ff_1_qn));  // open: preset, reset, en
  T_Flip_Flop t_ff_4 (.clk(C), .T(1'b1), .Q(Q0), .Qn(t_ff_4_qn), .reset(and_2_out));  // open: preset, en
  D_Flip_Flop d_ff_5 (.clk(d_ff_2_qn), .D(d_ff_5_qn), .Q(Q1_2), .Qn(d_ff_5_qn), .reset(and_3_out));  // open: preset, en
  J_K_Flip_Flop j_k_ff_4 (
    .J(j_k_ff_4_qn), .clk(j_k_ff_1_qn), .K(Q1_3), .Q(Q1_3), .Qn(j_k_ff_4_qn), .preset(Cy));  // open: en, reset
  T_Flip_Flop t_ff_5 (.clk(t_ff_1_qn), .T(1'b1), .Q(Q1_4), .Qn(t_ff_5_qn), .preset(Cy_2));  // open: reset, en
  J_K_Flip_Flop j_k_ff_5 (
    .J(j_k_ff_5_qn), .clk(j_k_ff_2_qn), .K(Q1_5), .Q(Q1_5), .Qn(j_k_ff_5_qn), .reset(and_4_out));  // open: preset, en
  D_Flip_Flop d_ff_6 (.clk(d_ff_3_qn), .D(d_ff_6_qn), .Q(Q1_6), .Qn(d_ff_6_qn), .reset(Cy_3));  // open: preset, en
  T_Flip_Flop t_ff_6 (.clk(Q1_7), .T(1'b1), .Q(Q2_7), .preset(and_5_out));  // open: Qn, reset, en
  T_Flip_Flop t_ff_7 (.clk(Q0_7), .T(1'b1), .Q(Q1_7), .preset(and_5_out));  // open: Qn, reset, en
  D_Flip_Flop d_ff_7 (.clk(Q0_8), .D(d_ff_7_qn), .Q(Q1_8), .Qn(d_ff_7_qn), .preset(and_6_out));  // open: en, reset
  J_K_Flip_Flop j_k_ff_6 (
    .J(j_k_ff_6_qn), .clk(Q0_9), .K(Q1_9), .Q(Q1_9), .Qn(j_k_ff_6_qn), .preset(and_7_out));  // open: en, reset
  T_Flip_Flop t_ff_8 (.clk(Q1_10), .T(1'b1), .Q(Q2_10), .preset(and_1_out));  // open: Qn, reset, en
  T_Flip_Flop t_ff_9 (.clk(Q0_10), .T(1'b1), .Q(Q1_10), .preset(and_1_out));  // open: Qn, reset, en
  T_Flip_Flop t_ff_10 (.clk(t_ff_4_qn), .T(1'b1), .Q(Q1), .Qn(t_ff_10_qn), .reset(and_2_out));  // open: preset, en
  D_Flip_Flop d_ff_8 (.clk(d_ff_5_qn), .D(d_ff_8_qn), .Q(Q2_2), .Qn(d_ff_8_qn), .reset(and_3_out));  // open: preset, en
  J_K_Flip_Flop j_k_ff_7 (
    .J(j_k_ff_7_qn), .clk(j_k_ff_4_qn), .K(Q2_3), .Q(Q2_3), .Qn(j_k_ff_7_qn), .reset(Cy));  // open: preset, en
  T_Flip_Flop t_ff_11 (.clk(t_ff_5_qn), .T(1'b1), .Q(Q2_4), .Qn(t_ff_11_qn), .preset(Cy_2));  // open: reset, en
  J_K_Flip_Flop j_k_ff_8 (
    .J(j_k_ff_8_qn), .clk(j_k_ff_5_qn), .K(Q2_5), .Q(Q2_5), .Qn(j_k_ff_8_qn), .reset(and_4_out));  // open: preset, en
  D_Flip_Flop d_ff_9 (.clk(d_ff_6_qn), .D(d_ff_9_qn), .Q(Q2_6), .Qn(d_ff_9_qn), .preset(Cy_3));  // open: en, reset
  T_Flip_Flop t_ff_12 (.clk(Q2_7), .T(1'b1), .Q(Q3_6), .preset(and_5_out));  // open: Qn, reset, en
  D_Flip_Flop d_ff_10 (.clk(Q1_8), .D(d_ff_10_qn), .Q(Q2_8), .Qn(d_ff_10_qn), .preset(and_6_out));  // open: en, reset
  J_K_Flip_Flop j_k_ff_9 (
    .J(j_k_ff_9_qn), .clk(Q1_9), .K(Q2_9), .Q(Q2_9), .Qn(j_k_ff_9_qn), .preset(and_7_out));  // open: en, reset
  T_Flip_Flop t_ff_13 (.clk(Q2_10), .T(1'b1), .Q(Q3_9), .preset(and_1_out));  // open: Qn, reset, en
  J_K_Flip_Flop j_k_ff_10 (
    .J(j_k_ff_10_qn), .clk(in_4), .K(j_k_ff_10_q), .Q(j_k_ff_10_q), .Qn(j_k_ff_10_qn));  // open: preset, en, reset
  T_Flip_Flop t_ff_14 (.clk(t_ff_10_qn), .T(1'b1), .Q(Q2), .Qn(t_ff_14_qn), .reset(and_2_out));  // open: preset, en
  D_Flip_Flop d_ff_11 (
    .clk(d_ff_8_qn), .D(d_ff_11_qn), .Q(Q3_2), .Qn(d_ff_11_qn), .reset(and_3_out));  // open: preset, en
  T_Flip_Flop t_ff_15 (.clk(t_ff_11_qn), .T(1'b1), .Q(Q3_3), .reset(Cy_2));  // open: Qn, preset, en
  J_K_Flip_Flop j_k_ff_11 (
    .J(j_k_ff_11_qn), .clk(j_k_ff_8_qn), .K(Q3_4), .Q(Q3_4), .Qn(j_k_ff_11_qn), .reset(and_4_out));  // open: preset, en
  D_Flip_Flop d_ff_12 (.clk(d_ff_9_qn), .D(d_ff_12_qn), .Q(Q3_5), .Qn(d_ff_12_qn), .reset(Cy_3));  // open: preset, en
  T_Flip_Flop t_ff_16 (.clk(Q3_6), .T(1'b1), .Q(Q4), .preset(and_5_out));  // open: Qn, reset, en
  D_Flip_Flop d_ff_13 (.clk(Q2_8), .D(d_ff_13_qn), .Q(Q3_7), .Qn(d_ff_13_qn), .preset(and_6_out));  // open: en, reset
  D_Flip_Flop d_ff_14 (.clk(Q3_7), .D(d_ff_14_qn), .Q(Q4_2), .Qn(d_ff_14_qn), .preset(and_6_out));  // open: en, reset
  J_K_Flip_Flop j_k_ff_12 (
    .J(j_k_ff_12_qn), .clk(Q2_9), .K(Q3_8), .Q(Q3_8), .Qn(j_k_ff_12_qn), .preset(and_7_out));  // open: en, reset
  and and_1 (and_1_out, Q0_10, ~Q1_10, ~Q2_10, ~Q3_9);  // AND_Gate
  T_Flip_Flop t_ff_17 (.clk(in_2), .T(1'b1));  // open: Q, Qn, preset, reset, en
  and and_2 (and_2_out, Q3, Q1);
  T_Flip_Flop t_ff_18 (.clk(t_ff_14_qn), .T(1'b1), .Q(Q3), .reset(and_2_out));  // open: Qn, preset, en
  and and_3 (and_3_out, Q3_2, Q1_2);
  and and_4 (and_4_out, Q0_5, Q1_5, Q3_4);
  and and_5 (and_5_out, Q0_7, ~Q1_7, Q2_7, Q3_6, ~Q4);  // AND_Gate
  and and_6 (and_6_out, ~Q0_8, ~Q1_8, Q2_8, Q3_7, ~Q4_2);  // AND_Gate
  J_K_Flip_Flop j_k_ff_13 (
    .J(j_k_ff_13_qn), .clk(Q3_8), .K(Q4_3), .Q(Q4_3), .Qn(j_k_ff_13_qn), .preset(and_7_out));  // open: en, reset
  and and_7 (and_7_out, ~Q0_9, Q1_9, Q2_9, Q3_8, ~Q4_3);  // AND_Gate

  // Notes on the sheet:
  //   Cy означає C установки
  //   Лічильник це пристрій якого типу?
  //   Тут те саме тільки діапазон [31;13]
  //   Для здачі цієї роботи корисно розуміти
  //   Також чув питання поки здавали інші:
  //   Це єдиний варіант який банально працює, здаючи таке треба пояснити:
  //   1. Коефіцієнт рахунку визначає кількість станів лічильника
  //   Це пристрій послідовнісного типу, тобто пристрій з пам'яттю
  //   Цей віднімаючий лічильник працює по модулю 18, тобто має 18 станів від числа [31;14] 
  //   Тут знову те саме тільки діапазон [31;15] ну і тригери змінюється, але думаю помітили
  //   Майже те саме що варіант 10 тільки простіше і тут діапазон можливих станів [15;2]
  //   Тому тут 10/16 варіантів, шанс що випаде 62,5%     Удачі
  //   2. Загальний принцип того як кожен з тригерів перетворюється в лічильник
  //   або ж пристрій вихідний стан якого залежить від попередніх станів, а не лише від вхідних даних
  //   Варіант 2: Сумуючий лічильник з послідовним переносом з коефіцієнтом рахунку 10 на T тригерах 
  //   Варіант 3: Сумуючий лічильник з послідовним переносом з коефіцієнтом рахунку 10 на D тригерах 
  //   Варіант 6: Сумуючий лічильник з послідовним переносом з коефіцієнтом рахунку 11 на JK тригерах 
  //   Варіант 10: Віднімаючий лічильник з послідовним переносом з коефіцієнтом рахунку 18 на T тригерах 
  //   Варіант 11: Віднімаючий лічильник з послідовним переносом з коефіцієнтом рахунку 19 на D тригерах 
  //   Варіант 12: Віднімаючий лічильник з послідовним переносом з коефіцієнтом рахунку 17 на JK тригерах 
  //   Варіант 15: Віднімаючий лічильник з послідовним переносом з коефіцієнтом рахунку 14 на T тригерах 
  //   Варіант 5: Сумуючий лічильник з послідовним переносом з попередньою установкою в число 7 з коефіцієнтом рахунку 16 на T тригерах 
  //   Здавати віднімаючі з довільними коефіцієнтами на свій страх і ризик, це єдиний нормальний спосіб який працює хочаб
  //   Суто для того аби хоч мали уявлення що складаєте
  //   Варіант 4: Сумуючий лічильник з послідовним переносом з попередньою установкою в число 3 з коефіцієнтом рахунку 8 на JK тригерах 
  //   Варіант 8: Сумуючий лічильник з послідовним переносом з попередньою установкою в число 5 з коефіцієнтом рахунку 16 на D тригерах 
  //   Тут лише варіанти де не реверсивний лічильник, бо як скласти те що на курсі і близько не працює знає лише Булетацький і диявол, хоча на рахунок другого не факт
endmodule
