// Logisim project lab13.circ as structural Verilog: 6 circuits, main circuit sum var1
module sum_var1 (
  input  X,
  input  Y,
  input  Z,
  output P,
  output S
);

  wire and_1_out, and_2_out, and_3_out, and_4_out, and_5_out, and_6_out, and_7_out, not_1_out;

  and and_1 (and_1_out, X, Y);
  and and_2 (and_2_out, Y, Z);
  and and_3 (and_3_out, Z, X);
  nand nand_1 (P, ~and_1_out, ~and_2_out, ~and_3_out);  // NAND_Gate
  not not_1 (not_1_out, P);
  and and_4 (and_4_out, not_1_out, X);
  and and_5 (and_5_out, not_1_out, Y);
  and and_6 (and_6_out, not_1_out, Z);
  and and_7 (and_7_out, X, Y, Z);
  nand nand_2 (S, ~and_4_out, ~and_5_out, ~and_6_out, ~and_7_out);  // NAND_Gate

  // Notes on the sheet:
  //   Варіант 1: на  I, НЕ
endmodule

module sum_var2 (
  input  X,
  input  Y,
  input  Z,
  output P,
  output S
);

  wire nor_1_out, nor_2_out, nor_3_out, nor_4_out, nor_5_out, nor_6_out, nor_7_out, not_1_out;

  nor nor_1 (nor_1_out, ~X, ~Y);  // NOR_Gate
  nor nor_2 (nor_2_out, ~Y, ~Z);  // NOR_Gate
  nor nor_3 (nor_3_out, ~Z, ~X);  // NOR_Gate
  or or_1 (P, nor_1_out, nor_2_out, nor_3_out);
  not not_1 (not_1_out, P);
  nor nor_4 (nor_4_out, ~not_1_out, ~X);  // NOR_Gate
  nor nor_5 (nor_5_out, ~not_1_out, ~Y);  // NOR_Gate
  nor nor_6 (nor_6_out, ~not_1_out, ~Z);  // NOR_Gate
  nor nor_7 (nor_7_out, ~X, ~Y, ~Z);  // NOR_Gate
  or or_2 (S, nor_4_out, nor_5_out, nor_6_out, nor_7_out);

  // Notes on the sheet:
  //   Варіант 2: на  АБО, НЕ
endmodule

// sum
module sum_var3 (
  input  X,
  input  Y,
  input  Z,
  output P,
  output S
);

  wire and_1_out, and_2_out, and_3_out, and_4_out, and_5_out, and_6_out, and_7_out, not_1_out;

  and and_1 (and_1_out, X, Y);
  and and_2 (and_2_out, Y, Z);
  and and_3 (and_3_out, Z, X);
  or or_1 (P, and_1_out, and_2_out, and_3_out);
  not not_1 (not_1_out, P);
  and and_4 (and_4_out, not_1_out, X);
  and and_5 (and_5_out, not_1_out, Y);
  or or_2 (S, and_4_out, and_5_out, and_6_out, and_7_out);
  and and_6 (and_6_out, not_1_out, Z);
  and and_7 (and_7_out, X, Y, Z);

  // Notes on the sheet:
  //   Варіант 3: на АБО, I, НЕ
endmodule

module multi (
  input  X0,
  input  Y0,
  input  Y1,
  input  X1,
  output P0,
  output P1,
  output P2,
  output P3
);

  wire and_2_out, and_3_out, and_4_out, sum_var3_1_p;

  and and_1 (P0, X0, Y0);
  and and_2 (and_2_out, Y0, X1);
  and and_3 (and_3_out, X0, Y1);
  and and_4 (and_4_out, Y1, X1);
  sum_var3 sum_var3_1 (.X(and_2_out), .Y(1'b0), .Z(and_3_out), .P(sum_var3_1_p), .S(P1));
  sum_var3 sum_var3_2 (.X(1'b0), .Y(sum_var3_1_p), .Z(and_4_out), .P(P3), .S(P2));

  // Notes on the sheet:
  //   Просто помножувач один окремо для другого завдання
endmodule

module _1 (
  input  X0,
  input  Y0,
  input  Y1,
  input  Y0_2,
  input  X0_2,
  input  Y1_2,
  input  X1,
  input  X1_2,
  input  X0_3,
  input  Y0_3,
  input  Y1_3,
  input  Y0_4,
  input  X0_4,
  input  Y1_4,
  input  X1_3,
  input  X1_4,
  output P0,
  output P1,
  output P0_2,
  output P2,
  output P1_2,
  output P3,
  output P2_2,
  output P3_2,
  output P0_3,
  output P1_3,
  output P0_4,
  output P2_3,
  output P1_4,
  output P3_3,
  output P2_4,
  output P3_4
);

  wire and_2_out, and_3_out, and_4_out, and_6_out, and_7_out, and_8_out, nor_2_out, nor_3_out, nor_4_out,
       nor_6_out, nor_7_out, nor_8_out, sum_var3_1_p, sum_var3_2_p, sum_var3_5_p, sum_var3_7_p;

  and and_1 (P0, X0, Y0_2);
  and and_2 (and_2_out, Y0_2, X1);
  and and_3 (and_3_out, X0, Y1_2);
  and and_4 (and_4_out, Y1_2, X1);
  nor nor_1 (P0_3, ~X0_3, ~Y0_4);  // NOR_Gate
  nor nor_2 (nor_2_out, ~Y0_4, ~X1_3);  // NOR_Gate
  nor nor_3 (nor_3_out, ~X0_3, ~Y1_4);  // NOR_Gate
  nor nor_4 (nor_4_out, ~Y1_4, ~X1_3);  // NOR_Gate
  sum_var3 sum_var3_1 (.X(and_2_out), .Y(1'b0), .Z(and_3_out), .P(sum_var3_1_p), .S(P1));
  sum_var3 sum_var3_2 (.X(nor_2_out), .Y(1'b0), .Z(nor_3_out), .P(sum_var3_2_p), .S(P1_3));
  sum_var3 sum_var3_3 (.X(1'b0), .Y(sum_var3_1_p), .Z(and_4_out), .P(P3), .S(P2));
  sum_var3 sum_var3_4 (.X(1'b0), .Y(sum_var3_2_p), .Z(nor_4_out), .P(P3_3), .S(P2_3));
  and and_5 (P0_2, X0_2, Y0);
  and and_6 (and_6_out, Y0, X1_2);
  nor nor_5 (P0_4, ~X0_4, ~Y0_3);  // NOR_Gate
  nor nor_6 (nor_6_out, ~Y0_3, ~X1_4);  // NOR_Gate
  and and_7 (and_7_out, X0_2, Y1);
  and and_8 (and_8_out, X1_2, Y1);
  nor nor_7 (nor_7_out, ~X0_4, ~Y1_3);  // NOR_Gate
  nor nor_8 (nor_8_out, ~X1_4, ~Y1_3);  // NOR_Gate
  sum_var3 sum_var3_5 (.X(and_7_out), .Y(1'b0), .Z(and_6_out), .P(sum_var3_5_p), .S(P1_2));
  sum_var3 sum_var3_6 (.X(sum_var3_5_p), .Y(and_8_out), .Z(1'b0), .P(P3_2), .S(P2_2));
  sum_var3 sum_var3_7 (.X(nor_7_out), .Y(1'b0), .Z(nor_6_out), .P(sum_var3_7_p), .S(P1_4));
  sum_var3 sum_var3_8 (.X(sum_var3_7_p), .Y(nor_8_out), .Z(1'b0), .P(P3_4), .S(P2_4));

  // Notes on the sheet:
  //   На елментах I, НЕ
  //   На елментах АБО, НЕ
  //   Обидві схеми абсолютно однакові з точки зору логіки,просто першу зібрав гарніше а друга як на мудлі
  //   Перше завдання однакове в усіх варіантах, різниця лише в тому, будете використовувати I чи АБО
endmodule

module _2 (
  input  X0,
  input  X1,
  input  Y0,
  input  Y1,
  input  X2,
  input  X0_2,
  input  X1_2,
  input  Y0_2,
  input  Y1_2,
  input  Y2,
  input  X0_3,
  input  X1_3,
  input  Z0,
  input  Y0_3,
  input  Y1_3,
  input  Z1,
  output P0,
  output P1,
  output P2,
  output P3,
  output P4,
  output P0_2,
  output P1_2,
  output P2_2,
  output P3_2,
  output P4_2,
  output P0_3,
  output P1_3,
  output P2_3,
  output P3_3,
  output P4_3,
  output P5
);

  wire and_1_out, and_2_out, and_3_out, and_4_out, multi_1_p2, multi_1_p3, multi_2_p2, multi_2_p3,
       multi_3_p0, multi_3_p1, multi_3_p2, multi_3_p3, multi_4_p2, multi_4_p3, multi_5_p0, multi_5_p1,
       multi_5_p2, multi_5_p3, sum_var3_1_p, sum_var3_3_p, sum_var3_5_p, sum_var3_6_p, sum_var3_7_p;

  multi multi_1 (.X0(X0), .Y0(Y0), .Y1(Y1), .X1(X1), .P0(P0), .P1(P1), .P2(multi_1_p2), .P3(multi_1_p3));
  and and_1 (and_1_out, Y1, X2);
  and and_2 (and_2_out, X2, Y0);
  multi multi_2 (.X0(X0_2), .Y0(Y0_2), .Y1(Y1_2), .X1(X1_2), .P0(P0_2), .P1(P1_2), .P2(multi_2_p2), .P3(multi_2_p3));
  and and_3 (and_3_out, X0_2, Y2);
  and and_4 (and_4_out, Y2, X1_2);
  multi multi_3 (
    .X0(X0_3), .Y0(Y0_3), .Y1(Y1_3), .X1(X1_3), .P0(multi_3_p0), .P1(multi_3_p1), .P2(multi_3_p2),
    .P3(multi_3_p3));
  sum_var3 sum_var3_1 (.X(multi_1_p2), .Y(1'b0), .Z(and_2_out), .P(sum_var3_1_p), .S(P2));
  sum_var3 sum_var3_2 (.X(sum_var3_1_p), .Y(multi_1_p3), .Z(and_1_out), .P(P4), .S(P3));
  sum_var3 sum_var3_3 (.X(multi_2_p2), .Y(1'b0), .Z(and_3_out), .P(sum_var3_3_p), .S(P2_2));
  sum_var3 sum_var3_4 (.X(sum_var3_3_p), .Y(and_4_out), .Z(multi_2_p3), .P(P4_2), .S(P3_2));
  multi multi_4 (
    .X0(Z0), .Y0(multi_3_p0), .Y1(multi_3_p1), .X1(Z1), .P0(P0_3), .P1(P1_3), .P2(multi_4_p2), .P3(multi_4_p3));
  multi multi_5 (
    .X0(Z0), .Y0(multi_3_p2), .Y1(multi_3_p3), .X1(Z1), .P0(multi_5_p0), .P1(multi_5_p1), .P2(multi_5_p2),
    .P3(multi_5_p3));
  sum_var3 sum_var3_5 (.X(multi_4_p2), .Y(1'b0), .Z(multi_5_p0), .P(sum_var3_5_p), .S(P2_3));
  sum_var3 sum_var3_6 (.X(sum_var3_5_p), .Y(multi_4_p3), .Z(multi_5_p1), .P(sum_var3_6_p), .S(P3_3));
  sum_var3 sum_var3_7 (.X(sum_var3_6_p), .Y(multi_5_p2), .Z(1'b0), .P(sum_var3_7_p), .S(P4_3));
  sum_var3 sum_var3_8 (.X(sum_var3_7_p), .Y(1'b0), .Z(multi_5_p3), .S(P5));  // open: P

  // Notes on the sheet:
  //   Варіант 1
  //   Варіант 2
  //   Варіант 3
endmodule
