// Logisim project var1.circ as structural Verilog: 3 circuits, main circuit 1
module _1 (
  input  A0,
  input  A1,
  input  A2,
  input  X0,
  input  X1,
  input  X2,
  input  X3,
  input  X4,
  input  X5,
  input  X6,
  input  X7,
  output Y
);

  wire and_1_out, and_2_out, and_3_out, and_4_out, and_5_out, and_6_out, and_7_out, and_8_out, not_1_out,
       not_2_out, not_3_out;

  not not_1 (not_1_out, A0);
  not not_2 (not_2_out, A1);
  not not_3 (not_3_out, A2);
  and and_1 (and_1_out, X0, not_1_out, not_2_out, not_3_out);
  and and_2 (and_2_out, X1, A0, not_2_out, not_3_out);
  and and_3 (and_3_out, X2, not_1_out, A1, not_3_out);
  and and_4 (and_4_out, X3, A0, A1, not_3_out);
  and and_5 (and_5_out, X4, not_1_out, not_2_out, A2);
  and and_6 (and_6_out, X5, A0, not_2_out, A2);
  and and_7 (and_7_out, X6, not_1_out, A1, A2);
  and and_8 (and_8_out, X7, A0, A1, A2);
  or or_1 (Y, and_1_out, and_2_out, and_3_out, and_4_out, and_5_out, and_6_out, and_7_out, and_8_out);
endmodule

module _2 (
  input  X1,
  input  X2,
  output Y0
);

  Multiplexer #(.select(2), .disabled(0), .enable("false")) multiplexer_1 (
    .in0(1'b1), .in1(1'b1), .in2(1'b1), .in3(1'b1), .out(Y0), .sel({X2, X1}));
endmodule

module _3 (
  input  A0,
  input  X,
  input  A1,
  input  A2,
  output Y0,
  output Y1,
  output Y2,
  output Y3,
  output Y4,
  output Y5,
  output Y6,
  output Y7
);

  wire not_1_out, not_2_out, not_3_out;

  not not_1 (not_1_out, A0);
  not not_2 (not_2_out, A1);
  not not_3 (not_3_out, A2);
  nor nor_1 (Y0, ~X, ~not_1_out, ~not_2_out, ~not_3_out);  // NOR_Gate
  nor nor_2 (Y1, ~X, ~A0, ~not_2_out, ~not_3_out);  // NOR_Gate
  nor nor_3 (Y2, ~X, ~not_1_out, ~A1, ~not_3_out);  // NOR_Gate
  nor nor_4 (Y3, ~X, ~A0, ~A1, ~not_3_out);  // NOR_Gate
  nor nor_5 (Y4, ~X, ~not_1_out, ~not_2_out, ~A2);  // NOR_Gate
  nor nor_6 (Y5, ~X, ~A0, ~not_2_out, ~A2);  // NOR_Gate
  nor nor_7 (Y6, ~X, ~not_1_out, ~A1, ~A2);  // NOR_Gate
  nor nor_8 (Y7, ~X, ~A0, ~A1, ~A2);  // NOR_Gate
endmodule
