// Logisim project var1.circ as structural Verilog: 2 circuits, main circuit 1
module _1 (
  input  X0,
  input  X1,
  input  X2,
  input  X3,
  output Y0,
  output Y1,
  output Y2,
  output Y3
);

  wire decoder_1_out1, decoder_1_out2, decoder_1_out3, decoder_1_out4, decoder_1_out5, decoder_1_out6,
       decoder_1_out7, decoder_1_out8, decoder_1_out9, decoder_1_out10, decoder_1_out11, decoder_1_out12,
       decoder_1_out13, decoder_1_out14;

  Decoder #(.select(4)) decoder_1 (
    .out1(decoder_1_out1), .out2(decoder_1_out2), .out3(decoder_1_out3), .out4(decoder_1_out4),
    .out5(decoder_1_out5), .out6(decoder_1_out6), .out7(decoder_1_out7), .out8(decoder_1_out8),
    .out9(decoder_1_out9), .out10(decoder_1_out10), .out11(decoder_1_out11), .out12(decoder_1_out12),
    .out13(decoder_1_out13), .out14(decoder_1_out14), .sel({X3, X2, X1, X0}), .en(1'b1));  // open: out0, out15
  or or_1 (Y0, decoder_1_out1, decoder_1_out3, decoder_1_out5, decoder_1_out8, decoder_1_out10, decoder_1_out12, decoder_1_out13, decoder_1_out14);
  or or_2 (Y1, decoder_1_out2, decoder_1_out3, decoder_1_out6, decoder_1_out9, decoder_1_out10, decoder_1_out14);
  or or_3 (Y2, decoder_1_out4, decoder_1_out5, decoder_1_out6, decoder_1_out11, decoder_1_out12, decoder_1_out13, decoder_1_out14);
  or or_4 (Y3, decoder_1_out7, decoder_1_out8, decoder_1_out9, decoder_1_out10, decoder_1_out11, decoder_1_out12, decoder_1_out13, decoder_1_out14);
endmodule

module _2 (
  input  X0,
  input  X1,
  input  X2,
  input  X3
);

  wire and_1_out, and_2_out, and_3_out, and_4_out, and_5_out, and_6_out, and_7_out, and_8_out, and_9_out,
       and_10_out, nand_1_out, nand_2_out, nand_3_out, nand_4_out, nand_5_out, nand_6_out, nand_7_out,
       not_1_out, not_2_out, not_3_out, not_4_out;

  not not_1 (not_1_out, X2);
  not not_2 (not_2_out, X3);
  not not_3 (not_3_out, X0);
  not not_4 (not_4_out, X1);
  and and_1 (and_1_out, not_3_out, not_4_out, not_1_out, not_2_out);
  and and_2 (and_2_out, X0, not_4_out, not_1_out, not_2_out);
  and and_3 (and_3_out, not_3_out, X1, not_1_out, not_2_out);
  and and_4 (and_4_out, X0, X1, not_1_out, not_2_out);
  and and_5 (and_5_out, not_3_out, not_4_out, X2, not_2_out);
  and and_6 (and_6_out, X0, not_4_out, X2, not_2_out);
  and and_7 (and_7_out, not_3_out, X1, X2, not_2_out);
  and and_8 (and_8_out, X0, X1, X2, not_2_out);
  and and_9 (and_9_out, not_3_out, not_4_out, not_1_out, X3);
  and and_10 (and_10_out, X0, not_4_out, not_1_out, X3);
  nand nand_1 (nand_1_out, ~and_1_out, ~and_3_out, ~and_4_out, ~and_6_out, ~and_7_out, ~and_8_out, ~and_9_out, ~and_10_out);  // NAND_Gate
  nand nand_2 (nand_2_out, ~and_1_out, ~and_2_out, ~and_3_out, ~and_4_out, ~and_5_out, ~and_8_out, ~and_9_out, ~and_10_out);  // NAND_Gate
  nand nand_3 (nand_3_out, ~and_1_out, ~and_2_out, ~and_4_out, ~and_5_out, ~and_6_out, ~and_7_out, ~and_8_out, ~and_9_out, ~and_10_out);  // NAND_Gate
  nand nand_4 (nand_4_out, ~and_1_out, ~and_3_out, ~and_4_out, ~and_6_out, ~and_7_out, ~and_9_out, ~and_10_out);  // NAND_Gate
  nand nand_5 (nand_5_out, ~and_1_out, ~and_3_out, ~and_7_out, ~and_9_out);  // NAND_Gate
  nand nand_6 (nand_6_out, ~and_1_out, ~and_5_out, ~and_6_out, ~and_7_out, ~and_9_out, ~and_10_out);  // NAND_Gate
  nand nand_7 (nand_7_out, ~and_3_out, ~and_4_out, ~and_5_out, ~and_6_out, ~and_7_out, ~and_9_out, ~and_10_out);  // NAND_Gate
  _7_Segment_Display u_7_segment_display_1 (
    .g(nand_7_out), .f(nand_6_out), .a(nand_1_out), .b(nand_2_out), .e(nand_5_out), .d(nand_4_out),
    .c(nand_3_out));  // open: dp
endmodule
