// Logisim project var2.circ as structural Verilog: 2 circuits, main circuit 1
module _1 (
  input  X0,
  input  X1,
  input  X2,
  input  X3,
  output Y0,
  output Y1,
  output Y2,
  output Y3
);

  wire decoder_1_out1, decoder_1_out2, decoder_1_out3, decoder_1_out4, decoder_1_out5, decoder_1_out6,
       decoder_1_out7, decoder_1_out8, decoder_1_out9, decoder_1_out10, decoder_1_out11, decoder_1_out12;

  Decoder #(.select(4)) decoder_1 (
    .out1(decoder_1_out1), .out2(decoder_1_out2), .out3(decoder_1_out3), .out4(decoder_1_out4),
    .out5(decoder_1_out5), .out6(decoder_1_out6), .out7(decoder_1_out7), .out8(decoder_1_out8),
    .out9(decoder_1_out9), .out10(decoder_1_out10), .out11(decoder_1_out11), .out12(decoder_1_out12),
    .sel({X3, X2, X1, X0}), .en(1'b1));  // open: out0, out13, out14, out15
  or or_1 (Y0, decoder_1_out1, decoder_1_out3, decoder_1_out6, decoder_1_out8, decoder_1_out10, decoder_1_out12);
  or or_2 (Y1, decoder_1_out2, decoder_1_out3, decoder_1_out7, decoder_1_out8, decoder_1_out11, decoder_1_out12);
  or or_3 (Y2, decoder_1_out4, decoder_1_out9, decoder_1_out10, decoder_1_out11, decoder_1_out12);
  or or_4 (Y3, decoder_1_out5, decoder_1_out6, decoder_1_out7, decoder_1_out8, decoder_1_out9, decoder_1_out10, decoder_1_out11, decoder_1_out12);
endmodule

module _2 (
  input  X0,
  input  X1,
  input  X2,
  input  X3
);

  wire nor_1_out, nor_2_out, nor_3_out, nor_4_out, nor_5_out, nor_6_out, nor_7_out, nor_8_out, nor_9_out,
       nor_10_out, not_1_out, not_2_out, not_3_out, not_4_out, or_1_out, or_2_out, or_3_out, or_4_out,
       or_5_out, or_6_out, or_7_out;

  not not_1 (not_1_out, X2);
  not not_2 (not_2_out, X3);
  not not_3 (not_3_out, X0);
  not not_4 (not_4_out, X1);
  nor nor_1 (nor_1_out, ~not_3_out, ~not_4_out, ~not_1_out, ~not_2_out);  // NOR_Gate
  nor nor_2 (nor_2_out, ~X0, ~not_4_out, ~not_1_out, ~not_2_out);  // NOR_Gate
  nor nor_3 (nor_3_out, ~not_3_out, ~X1, ~not_1_out, ~not_2_out);  // NOR_Gate
  nor nor_4 (nor_4_out, ~X0, ~X1, ~not_1_out, ~not_2_out);  // NOR_Gate
  nor nor_5 (nor_5_out, ~not_3_out, ~not_4_out, ~X2, ~not_2_out);  // NOR_Gate
  nor nor_6 (nor_6_out, ~X0, ~not_4_out, ~X2, ~not_2_out);  // NOR_Gate
  nor nor_7 (nor_7_out, ~not_3_out, ~X1, ~X2, ~not_2_out);  // NOR_Gate
  nor nor_8 (nor_8_out, ~X0, ~X1, ~X2, ~not_2_out);  // NOR_Gate
  nor nor_9 (nor_9_out, ~not_3_out, ~not_4_out, ~not_1_out, ~X3);  // NOR_Gate
  nor nor_10 (nor_10_out, ~X0, ~not_4_out, ~not_1_out, ~X3);  // NOR_Gate
  or or_1 (or_1_out, nor_1_out, nor_3_out, nor_4_out, nor_6_out, nor_7_out, nor_8_out, nor_9_out, nor_10_out);
  or or_2 (or_2_out, nor_1_out, nor_2_out, nor_3_out, nor_4_out, nor_5_out, nor_8_out, nor_9_out, nor_10_out);
  or or_3 (or_3_out, nor_1_out, nor_2_out, nor_4_out, nor_5_out, nor_6_out, nor_7_out, nor_8_out, nor_9_out, nor_10_out);
  or or_4 (or_4_out, nor_1_out, nor_3_out, nor_4_out, nor_6_out, nor_7_out, nor_9_out, nor_10_out);
  or or_5 (or_5_out, nor_1_out, nor_3_out, nor_7_out, nor_9_out);
  or or_6 (or_6_out, nor_1_out, nor_5_out, nor_6_out, nor_7_out, nor_9_out, nor_10_out);
  or or_7 (or_7_out, nor_3_out, nor_4_out, nor_5_out, nor_6_out, nor_7_out, nor_9_out, nor_10_out);
  _7_Segment_Display u_7_segment_display_1 (
    .g(or_7_out), .f(or_6_out), .a(or_1_out), .b(or_2_out), .e(or_5_out), .d(or_4_out), .c(or_3_out));  // open: dp
endmodule
