// Logisim project var1.circ as structural Verilog: 3 circuits, main circuit 1
module _1 (
  input  A0,
  input  B0,
  input  A1,
  input  B1,
  output Y
);

  wire xnor_1_out, xnor_2_out;

  xnor xnor_1 (xnor_1_out, A0, B0);
  xnor xnor_2 (xnor_2_out, A1, B1);
  and and_1 (Y, xnor_1_out, xnor_2_out);
endmodule

module _2 (
  input  A0,
  input  B0,
  input  A1,
  input  B1,
  input  A2,
  input  B2,
  output a_b,
  output a_b_2,
  output a_b_3
);

  wire and_1_out, and_2_out, and_3_out, and_4_out, and_5_out, and_6_out, and_7_out, and_8_out, and_9_out,
       and_10_out, xnor_1_out, xnor_2_out, xnor_3_out;

  and and_1 (and_1_out, ~A0, B0);  // AND_Gate
  and and_2 (and_2_out, ~A1, B1);  // AND_Gate
  and and_3 (and_3_out, ~A2, B2);  // AND_Gate
  xnor xnor_1 (xnor_1_out, A0, B0);
  xnor xnor_2 (xnor_2_out, A1, B1);
  xnor xnor_3 (xnor_3_out, A2, B2);
  and and_4 (and_4_out, ~B2, A2);  // AND_Gate
  and and_5 (and_5_out, ~B1, A1);  // AND_Gate
  and and_6 (and_6_out, ~B0, A0);  // AND_Gate
  and and_7 (and_7_out, and_1_out, ~and_5_out, ~and_4_out);  // AND_Gate
  and and_8 (and_8_out, and_2_out, ~and_4_out);  // AND_Gate
  and and_9 (and_9_out, ~and_3_out, and_5_out);  // AND_Gate
  and and_10 (and_10_out, ~and_3_out, ~and_2_out, and_6_out);  // AND_Gate
  or or_1 (a_b, and_7_out, and_8_out, and_3_out);
  and and_11 (a_b_2, xnor_1_out, xnor_2_out, xnor_3_out);
  or or_2 (a_b_3, and_4_out, and_9_out, and_10_out);
endmodule

module _3 (
  input  A0,
  input  A1,
  input  A2,
  input  B0,
  input  B1,
  input  B2,
  input  C0,
  input  C1,
  input  C2,
  output A,
  output B,
  output C
);

  wire n2_1_a_b, n2_1_a_b_3, n2_2_a_b, n2_2_a_b_3, n2_3_a_b, n2_3_a_b_3;

  _2 u_2_1 (.A0(A0), .B0(B0), .A1(A1), .B1(B1), .A2(A2), .B2(B2), .a_b(n2_1_a_b), .a_b_3(n2_1_a_b_3));  // open: a_b_2
  _2 u_2_2 (.A0(A0), .B0(C0), .A1(A1), .B1(C1), .A2(A2), .B2(C2), .a_b(n2_2_a_b), .a_b_3(n2_2_a_b_3));  // open: a_b_2
  _2 u_2_3 (.A0(B0), .B0(C0), .A1(B1), .B1(C1), .A2(B2), .B2(C2), .a_b(n2_3_a_b), .a_b_3(n2_3_a_b_3));  // open: a_b_2
  and and_1 (A, n2_1_a_b_3, n2_2_a_b_3);
  and and_2 (B, n2_1_a_b, n2_3_a_b_3);
  and and_3 (C, n2_2_a_b, n2_3_a_b);
endmodule
