// Logisim project var7.circ as structural Verilog: 3 circuits, main circuit 1
// sum
module _1 (
  input  x,
  input  y,
  input  z,
  output p,
  output s
);

  wire and_1_out, and_2_out, and_3_out, and_4_out, and_5_out, and_6_out, and_7_out, not_1_out;

  and and_1 (and_1_out, x, y);
  nand nand_1 (p, ~and_1_out, ~and_2_out, ~and_3_out);  // NAND_Gate
  and and_2 (and_2_out, x, z);
  and and_3 (and_3_out, y, z);
  not not_1 (not_1_out, p);
  and and_4 (and_4_out, not_1_out, x);
  and and_5 (and_5_out, not_1_out, y);
  and and_6 (and_6_out, not_1_out, z);
  and and_7 (and_7_out, x, y, z);
  nand nand_2 (s, ~and_4_out, ~and_5_out, ~and_6_out, ~and_7_out);  // NAND_Gate
endmodule

// SK
module _2 (
  input  x0,
  input  x1,
  input  y0,
  input  y1,
  output s0,
  output s1,
  output s2
);

  wire and_1_out;

  and and_1 (and_1_out, x0, y0);
  _1 u_1_1 (.x(x0), .y(y0), .z(1'b0), .s(s0));  // open: p
  _1 u_1_2 (.x(x1), .y(y1), .z(and_1_out), .p(s2), .s(s1));
endmodule

module _3 (
  input  x0,
  input  x1,
  input  y0,
  input  y1,
  output s0,
  output s1
);

  wire not_1_out, not_2_out, or_1_out;

  not not_1 (not_1_out, y0);
  not not_2 (not_2_out, y1);
  _1 u_1_1 (.x(x0), .y(not_1_out), .z(1'b1), .s(s0));  // open: p
  _1 u_1_2 (.x(x1), .y(not_2_out), .z(or_1_out), .s(s1));  // open: p
  or or_1 (or_1_out, x0, not_1_out);
endmodule
