// Logisim project lab9.circ as structural Verilog: 2 circuits, main circuit 3
module _3 (
  input  C,
  input  Xr,
  input  V,
  input  Xl,
  input  C_2,
  input  Xr_2,
  input  V_2,
  input  Xl_2,
  input  C_3,
  input  Xr_3,
  input  V_3,
  input  Xl_3,
  output Q0,
  output Q1,
  output Q2,
  output Q3,
  output Q0_2,
  output Q1_2,
  output Q2_2,
  output Q3_2,
  output Q0_3,
  output Q1_3,
  output Q2_3,
  output Q3_3
);

  wire and_1_out, and_2_out, and_3_out, and_4_out, and_5_out, and_6_out, and_7_out, and_8_out, and_9_out,
       and_10_out, and_11_out, and_12_out, and_13_out, and_14_out, and_15_out, and_16_out, and_17_out,
       and_18_out, and_19_out, and_20_out, and_21_out, and_22_out, and_23_out, and_24_out, d_ff_2_q,
       d_ff_3_q, d_ff_5_q, d_ff_6_q, d_ff_8_q, d_ff_9_q, d_ff_11_q, d_ff_12_q, not_1_out, not_2_out,
       not_3_out, or_1_out, or_2_out, or_3_out, or_4_out, or_5_out, or_6_out, or_7_out, or_8_out, or_9_out,
       or_10_out, or_11_out, or_12_out;

  and and_1 (and_1_out, V, Q1);
  and and_2 (and_2_out, Xl, not_1_out);
  not not_1 (not_1_out, V);
  and and_3 (and_3_out, V_2, d_ff_5_q);
  and and_4 (and_4_out, Xl_2, not_2_out);
  not not_2 (not_2_out, V_2);
  and and_5 (and_5_out, V_3, d_ff_6_q);
  and and_6 (and_6_out, Xl_3, not_3_out);
  not not_3 (not_3_out, V_3);
  or or_1 (or_1_out, and_1_out, and_2_out);
  or or_2 (or_2_out, and_3_out, and_4_out);
  or or_3 (or_3_out, and_5_out, and_6_out);
  and and_7 (and_7_out, Q2, V);
  D_Flip_Flop d_ff_1 (.clk(C), .D(or_1_out), .Q(Q0));  // open: Qn, preset, en, reset
  and and_8 (and_8_out, Q0, not_1_out);
  and and_9 (and_9_out, d_ff_8_q, V_2);
  D_Flip_Flop d_ff_2 (.clk(C_2), .D(or_2_out), .Q(d_ff_2_q));  // open: Qn, preset, en, reset
  and and_10 (and_10_out, d_ff_2_q, not_2_out);
  not not_4 (Q0_2, d_ff_2_q);
  and and_11 (and_11_out, d_ff_9_q, V_3);
  D_Flip_Flop d_ff_3 (.clk(C_3), .D(or_3_out), .Q(d_ff_3_q));  // open: Qn, preset, en, reset
  and and_12 (and_12_out, d_ff_3_q, not_3_out);
  not not_5 (Q0_3, d_ff_3_q);
  or or_4 (or_4_out, and_7_out, and_8_out);
  or or_5 (or_5_out, and_9_out, and_10_out);
  or or_6 (or_6_out, and_11_out, and_12_out);
  D_Flip_Flop d_ff_4 (.clk(C), .D(or_4_out), .Q(Q1));  // open: Qn, preset, en, reset
  D_Flip_Flop d_ff_5 (.clk(C_2), .D(or_5_out), .Q(d_ff_5_q));  // open: Qn, preset, en, reset
  not not_6 (Q1_2, d_ff_5_q);
  D_Flip_Flop d_ff_6 (.clk(C_3), .D(or_6_out), .Q(d_ff_6_q));  // open: Qn, preset, en, reset
  not not_7 (Q1_3, d_ff_6_q);
  and and_13 (and_13_out, Q3, V);
  or or_7 (or_7_out, and_13_out, and_14_out);
  and and_14 (and_14_out, Q1, not_1_out);
  and and_15 (and_15_out, d_ff_11_q, V_2);
  or or_8 (or_8_out, and_15_out, and_16_out);
  and and_16 (and_16_out, d_ff_5_q, not_2_out);
  and and_17 (and_17_out, d_ff_12_q, V_3);
  or or_9 (or_9_out, and_17_out, and_18_out);
  and and_18 (and_18_out, d_ff_6_q, not_3_out);
  D_Flip_Flop d_ff_7 (.clk(C), .D(or_7_out), .Q(Q2));  // open: Qn, preset, en, reset
  D_Flip_Flop d_ff_8 (.clk(C_2), .D(or_8_out), .Q(d_ff_8_q));  // open: Qn, preset, en, reset
  not not_8 (Q2_2, d_ff_8_q);
  D_Flip_Flop d_ff_9 (.clk(C_3), .D(or_9_out), .Q(d_ff_9_q));  // open: Qn, preset, en, reset
  not not_9 (Q2_3, d_ff_9_q);
  and and_19 (and_19_out, Xr, V);
  or or_10 (or_10_out, and_19_out, and_20_out);
  and and_20 (and_20_out, Q2, not_1_out);
  and and_21 (and_21_out, Xr_2, V_2);
  or or_11 (or_11_out, and_21_out, and_22_out);
  and and_22 (and_22_out, d_ff_8_q, not_2_out);
  and and_23 (and_23_out, Xr_3, V_3);
  or or_12 (or_12_out, and_23_out, and_24_out);
  and and_24 (and_24_out, d_ff_9_q, not_3_out);
  D_Flip_Flop d_ff_10 (.clk(C), .D(or_10_out), .Q(Q3));  // open: Qn, preset, en, reset
  D_Flip_Flop d_ff_11 (.clk(C_2), .D(or_11_out), .Q(d_ff_11_q));  // open: Qn, preset, en, reset
  not not_10 (Q3_2, d_ff_11_q);
  D_Flip_Flop d_ff_12 (.clk(C_3), .D(or_12_out), .Q(d_ff_12_q));  // open: Qn, preset, en, reset
  not not_11 (Q3_3, d_ff_12_q);

  // Notes on the sheet:
  //   Чотирирозрядний послідовний реверсивний регістр на D-тригерах  з видачею іформації в прямому коді
  //   Чотирирозрядний послідовний реверсивний регістр на D-тригерах з видачею інформації в оберненому коді
  //   Чотирирозрядний послідовний реверсивний регістр на RS-тригерах з видачею інформації в оберненому коді
endmodule

module _4 (
  input  C,
  input  Xr,
  input  V,
  input  Xl,
  input  \Cч ,
  input  C_2,
  input  Xr_2,
  input  V_2,
  input  Xl_2,
  input  \Cч_2 ,
  output Q0,
  output Q1,
  output Q2,
  output Q3,
  output Q0_2,
  output Q1_2,
  output Q2_2,
  output Q3_2
);

  wire and_1_out, and_2_out, and_3_out, and_4_out, and_5_out, and_6_out, and_8_out, and_9_out, and_13_out,
       and_14_out, and_15_out, and_16_out, and_17_out, and_18_out, and_20_out, and_21_out, d_ff_1_q,
       d_ff_2_q, d_ff_3_q, d_ff_4_q, d_ff_5_q, d_ff_6_q, d_ff_7_q, d_ff_8_q, not_1_out, not_2_out, or_1_out,
       or_2_out, or_3_out, or_4_out, or_5_out, or_6_out, or_7_out, or_8_out;

  and and_1 (and_1_out, V, d_ff_3_q);
  and and_2 (and_2_out, Xl, not_1_out);
  not not_1 (not_1_out, V);
  and and_3 (and_3_out, V_2, d_ff_4_q);
  and and_4 (and_4_out, Xl_2, not_2_out);
  not not_2 (not_2_out, V_2);
  or or_1 (or_1_out, and_1_out, and_2_out);
  or or_2 (or_2_out, and_3_out, and_4_out);
  and and_5 (and_5_out, d_ff_5_q, V);
  D_Flip_Flop d_ff_1 (.clk(C), .D(or_1_out), .Q(d_ff_1_q));  // open: Qn, preset, en, reset
  and and_6 (and_6_out, d_ff_1_q, not_1_out);
  and and_7 (Q0, d_ff_1_q, \Cч );
  and and_8 (and_8_out, d_ff_6_q, V_2);
  D_Flip_Flop d_ff_2 (.clk(C_2), .D(or_2_out), .Q(d_ff_2_q));  // open: Qn, preset, en, reset
  and and_9 (and_9_out, d_ff_2_q, not_2_out);
  and and_10 (Q0_2, ~d_ff_2_q, \Cч_2 );  // AND_Gate
  or or_3 (or_3_out, and_5_out, and_6_out);
  or or_4 (or_4_out, and_8_out, and_9_out);
  D_Flip_Flop d_ff_3 (.clk(C), .D(or_3_out), .Q(d_ff_3_q));  // open: Qn, preset, en, reset
  and and_11 (Q1, d_ff_3_q, \Cч );
  D_Flip_Flop d_ff_4 (.clk(C_2), .D(or_4_out), .Q(d_ff_4_q));  // open: Qn, preset, en, reset
  and and_12 (Q1_2, ~d_ff_4_q, \Cч_2 );  // AND_Gate
  and and_13 (and_13_out, d_ff_7_q, V);
  or or_5 (or_5_out, and_13_out, and_14_out);
  and and_14 (and_14_out, d_ff_3_q, not_1_out);
  and and_15 (and_15_out, d_ff_8_q, V_2);
  or or_6 (or_6_out, and_15_out, and_16_out);
  and and_16 (and_16_out, d_ff_4_q, not_2_out);
  D_Flip_Flop d_ff_5 (.clk(C), .D(or_5_out), .Q(d_ff_5_q));  // open: Qn, preset, en, reset
  D_Flip_Flop d_ff_6 (.clk(C_2), .D(or_6_out), .Q(d_ff_6_q));  // open: Qn, preset, en, reset
  and and_17 (and_17_out, Xr, V);
  or or_7 (or_7_out, and_17_out, and_18_out);
  and and_18 (and_18_out, d_ff_5_q, not_1_out);
  and and_19 (Q2, d_ff_5_q, \Cч );
  and and_20 (and_20_out, Xr_2, V_2);
  or or_8 (or_8_out, and_20_out, and_21_out);
  and and_21 (and_21_out, d_ff_6_q, not_2_out);
  and and_22 (Q2_2, ~d_ff_6_q, \Cч_2 );  // AND_Gate
  D_Flip_Flop d_ff_7 (.clk(C), .D(or_7_out), .Q(d_ff_7_q));  // open: Qn, preset, en, reset
  D_Flip_Flop d_ff_8 (.clk(C_2), .D(or_8_out), .Q(d_ff_8_q));  // open: Qn, preset, en, reset
  and and_23 (Q3, d_ff_7_q, \Cч );
  and and_24 (Q3_2, ~d_ff_8_q, \Cч_2 );  // AND_Gate

  // Notes on the sheet:
  //   Чотирирозрядний послідовний реверсивний регістр на D-тригерах  з паралельною видачею іформації в прямому коді
  //   Чотирирозрядний послідовний реверсивний регістр на D-тригерах  з паралельною видачею іформації в прямому коді
endmodule
