// Logisim project var7.circ as structural Verilog: 1 circuit, main circuit 3
module _3 (
  input  S3,
  input  S2,
  input  S1,
  input  S0,
  input  B3,
  input  A3,
  input  B2,
  input  A2,
  input  B1,
  input  A1,
  input  B0,
  input  A0,
  input  M,
  input  Cn_prime,
  output G,
  output Cn_4_prime,
  output P,
  output F3,
  output F2,
  output A_B,
  output F1,
  output F0
);

  wire and_1_out, and_2_out, and_3_out, and_4_out, and_5_out, and_6_out, and_7_out, and_8_out, and_9_out,
       and_10_out, and_11_out, and_12_out, and_13_out, and_14_out, and_15_out, and_16_out, and_17_out,
       and_18_out, and_19_out, and_20_out, and_21_out, and_22_out, and_23_out, and_24_out, and_25_out,
       and_26_out, and_27_out, and_28_out, buffer_1_out, buffer_2_out, buffer_3_out, buffer_4_out,
       buffer_5_out, nand_1_out, nand_3_out, nor_1_out, nor_2_out, nor_3_out, nor_4_out, nor_5_out,
       nor_6_out, nor_7_out, nor_8_out, nor_10_out, nor_11_out, not_1_out, xor_1_out, xor_2_out, xor_3_out,
       xor_4_out;

  not not_1 (not_1_out, M);
  and and_1 (and_1_out, B3, A3, S3);
  and and_2 (and_2_out, ~B3, A3, S2);  // AND_Gate
  and and_3 (and_3_out, ~B3, S1);  // AND_Gate
  and and_4 (and_4_out, B3, S0);
  buf buffer_1 (buffer_1_out, A3);
  and and_5 (and_5_out, B2, A2, S3);
  and and_6 (and_6_out, ~B2, A2, S2);  // AND_Gate
  and and_7 (and_7_out, ~B2, S1);  // AND_Gate
  and and_8 (and_8_out, B2, S0);
  buf buffer_2 (buffer_2_out, A2);
  and and_9 (and_9_out, B1, A1, S3);
  and and_10 (and_10_out, ~B1, A1, S2);  // AND_Gate
  and and_11 (and_11_out, ~B1, S1);  // AND_Gate
  and and_12 (and_12_out, B1, S0);
  buf buffer_3 (buffer_3_out, A1);
  and and_13 (and_13_out, B0, A0, S3);
  and and_14 (and_14_out, ~B0, A0, S2);  // AND_Gate
  and and_15 (and_15_out, ~B0, S1);  // AND_Gate
  and and_16 (and_16_out, B0, S0);
  buf buffer_4 (buffer_4_out, A0);
  nor nor_1 (nor_1_out, and_1_out, and_2_out);
  nor nor_2 (nor_2_out, and_3_out, buffer_1_out);
  nor nor_3 (nor_3_out, and_5_out, and_6_out);
  nor nor_4 (nor_4_out, and_7_out, buffer_2_out);
  nor nor_5 (nor_5_out, and_9_out, and_10_out);
  nor nor_6 (nor_6_out, and_11_out, buffer_3_out);
  nor nor_7 (nor_7_out, and_13_out, and_14_out);
  nor nor_8 (nor_8_out, and_15_out, buffer_4_out);
  nand nand_1 (nand_1_out, Cn_prime, nor_1_out, nor_7_out, nor_5_out, nor_3_out);
  nand nand_2 (P, nor_1_out, nor_7_out, nor_5_out, nor_3_out);
  and and_17 (and_17_out, nor_1_out, nor_5_out, nor_8_out, nor_3_out);
  and and_18 (and_18_out, nor_1_out, nor_6_out, nor_3_out);
  and and_19 (and_19_out, nor_1_out, nor_4_out);
  buf buffer_5 (buffer_5_out, nor_2_out);
  xor xor_1 (xor_1_out, nor_1_out, nor_2_out);
  and and_20 (and_20_out, nor_7_out, nor_5_out, nor_3_out, nor_7_out, not_1_out);
  and and_21 (and_21_out, nor_5_out, nor_8_out, nor_8_out, not_1_out);
  and and_22 (and_22_out, nor_3_out, nor_6_out, not_1_out);
  and and_23 (and_23_out, nor_4_out, not_1_out);
  xor xor_2 (xor_2_out, nor_3_out, nor_4_out);
  and and_24 (and_24_out, Cn_prime, nor_5_out, nor_7_out, not_1_out);
  and and_25 (and_25_out, nor_5_out, nor_8_out, not_1_out);
  and and_26 (and_26_out, nor_6_out, not_1_out);
  xor xor_3 (xor_3_out, nor_5_out, nor_6_out);
  and and_27 (and_27_out, Cn_prime, nor_7_out, not_1_out);
  and and_28 (and_28_out, nor_8_out, not_1_out);
  xor xor_4 (xor_4_out, nor_7_out, nor_8_out);
  nand nand_3 (nand_3_out, Cn_prime, not_1_out);
  nor nor_9 (G, and_17_out, and_18_out, and_19_out, buffer_5_out);
  nor nor_10 (nor_10_out, and_20_out, and_21_out, and_22_out, and_23_out);
  nor nor_11 (nor_11_out, and_24_out, and_25_out, and_26_out);
  nor nor_12 (xor_3_out, and_27_out, and_28_out);
  or or_1 (Cn_4_prime, ~nand_1_out, ~G);  // OR_Gate
  xor xor_5 (F3, xor_1_out, nor_10_out);
  xor xor_6 (F2, xor_2_out, nor_11_out);
  xor xor_7 (F1, xor_3_out, xor_3_out);
  xor xor_8 (F0, xor_4_out, nand_3_out);
  and and_29 (A_B, F3, F2, F1, F0);
endmodule
